# Fritzing sketch GPIO (saved by Fritzing 0.8.7b)
breadboards: 1

parts:
  BeagleBone1 = BeagleBone Black
  S1 = Pushbutton [package="[SMD]"]
  S2 = Pushbutton [package="[SMD]"]
  S3 = Pushbutton [package="[SMD]"]
  S4 = Pushbutton [package="[SMD]"]
  S5 = Pushbutton [package="[SMD]"]
  S6 = Pushbutton [package="[SMD]"]
  S7 = Pushbutton [package="[SMD]"]
  S8 = Pushbutton [package="[SMD]"]
  S9 = Pushbutton [package="[SMD]"]
  S10 = Pushbutton [package="[SMD]"]
  S11 = Pushbutton [package="[SMD]"]
  S12 = Pushbutton [package="[SMD]"]
  S13 = Pushbutton [package="[SMD]"]
  R1 = Resistor [tolerance=±5% resistance=10k package=THT]
  R2 = Resistor [tolerance=±5% resistance=10k package=THT]
  R3 = Resistor [tolerance=±5% resistance=10k package=THT]
  R4 = Resistor [tolerance=±5% resistance=10k package=THT]
  R5 = Resistor [tolerance=±5% resistance=10k package=THT]
  R6 = Resistor [tolerance=±5% resistance=10k package=THT]
  R7 = Resistor [tolerance=±5% resistance=10k package=THT]
  R8 = Resistor [tolerance=±5% resistance=10k package=THT]
  R9 = Resistor [tolerance=±5% resistance=10k package=THT]
  R10 = Resistor [tolerance=±5% resistance=10k package=THT]
  R11 = Resistor [tolerance=±5% resistance=10k package=THT]
  R12 = Resistor [tolerance=±5% resistance=10k package=THT]
  R13 = Resistor [tolerance=±5% resistance=10k package=THT]

nets:
  N1: BeagleBone1.no_name_yet#3, BeagleBone1.no_name_yet#4, S1.Pin_3, S1.Pin_4, S2.Pin_3, S2.Pin_4, S3.Pin_3, S3.Pin_4, S4.Pin_3, S4.Pin_4, S5.Pin_3, S5.Pin_4, S6.Pin_1, S6.Pin_2, S7.Pin_3, S7.Pin_4, S8.Pin_3, S8.Pin_4, S9.Pin_3, S9.Pin_4, S10.Pin_3, S10.Pin_4, S11.Pin_3, S11.Pin_4, S12.Pin_3, S12.Pin_4, S13.Pin_3, S13.Pin_4
  N2: BeagleBone1.no_name_yet#102, R1.Pin_0, R2.Pin_0, R3.Pin_0, R4.Pin_0, R5.Pin_0, R6.Pin_0, R7.Pin_0, R8.Pin_0, R9.Pin_0, R10.Pin_1, R11.Pin_1, R12.Pin_1, R13.Pin_1
  N3: BeagleBone1.no_name_yet#107, S1.Pin_1, S1.Pin_2, R4.Pin_1
  N4: BeagleBone1.no_name_yet#108, S2.Pin_1, S2.Pin_2, R5.Pin_1
  N5: BeagleBone1.no_name_yet#109, S3.Pin_1, S3.Pin_2, R6.Pin_1
  N6: BeagleBone1.no_name_yet#110, S4.Pin_1, S4.Pin_2, R7.Pin_1
  N7: BeagleBone1.no_name_yet#111, S6.Pin_3, S6.Pin_4, R9.Pin_1
  N8: BeagleBone1.no_name_yet#112, S7.Pin_1, S7.Pin_2, R3.Pin_1
  N9: BeagleBone1.no_name_yet#113, S10.Pin_1, S10.Pin_2, R10.Pin_0
  N10: BeagleBone1.no_name_yet#114, S11.Pin_1, S11.Pin_2, R11.Pin_0
  N11: BeagleBone1.no_name_yet#115, S12.Pin_1, S12.Pin_2, R12.Pin_0
  N12: BeagleBone1.no_name_yet#116, S13.Pin_1, S13.Pin_2, R13.Pin_0
  N13: BeagleBone1.no_name_yet#117, S8.Pin_1, S8.Pin_2, R2.Pin_1
  N14: BeagleBone1.no_name_yet#118, S9.Pin_1, S9.Pin_2, R1.Pin_1
  N15: BeagleBone1.no_name_yet#119, S5.Pin_1, S5.Pin_2, R8.Pin_1

custom parts:
  BeagleBone Black: BeagleBone Black rev. A5B
